# Fritzing sketch wiring (saved by Fritzing 0.9.3b)
breadboards: 1

parts:
  Part1 = INA219 High Side DC Current Sensor Breakout [part_number=904]
  Part2 = Arduino Pro Mini (5V)
  J1 = Generic female header - 2 pins [form="♀ (female)" package=THT]
  Part3 = TP4056 Charger
  J3 = SSD1306 128x64 [form="♂ (male)" package=THT]
  J4 = Step-Up-Converter [form="♀ (female)" package=THT]
  S1 = Pushbutton [package="[THT]"]

nets:
  N1: Part1.VIN-, Part3.BAT+
  N2: Part1.VIN+, J1.+
  VCC: Part1.VCC, Part2.VCC, J3.VCC, J4.pin3, S1.Pin_3, S1.Pin_4
  GND: Part1.GND, Part2.GND, J3.GND, J4.pin4
  N3: Part1.SCL, Part2.A4, J3.SCL
  N4: Part1.SDA, Part2.A5, J3.SDA
  N5: Part2.MISO, S1.Pin_1, S1.Pin_2
  N6: J1.-, Part3.BAT-, J4.pin1

custom parts:
  INA219 High Side DC Current Sensor Breakout: This breakout board will solve all your power-monitoring problems. Instead of struggling with two multimeters, you can just use the handy INA219B chip on this breakout to both measure both the high side voltage and DC current draw over I2C with 1% precision. Most current-measuring devices such as our current panel meter are only good for low side measuring. That means that unless you want to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
  Generic female header - 2 pins: Generic female header
  SSD1306 128x64: These displays are small, only about 1" diagonal, but very readable due to the high contrast of an OLED display. This display is made of 128x64 individual white OLED pixels, each one is turned on or off by the controller chip. Because the display makes its own light, no backlight is required. This reduces the power required to run the OLED and is why the display has such high contrast; we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
  Step-Up-Converter: Generic female header
